// Logisim project stack_logical_normal.circ as structural Verilog: 20 circuits, main circuit main
module main (
  input  CLK,
  input  RESET,
  input  [1:0] COMMAND,
  input  [2:0] INDEX,
  input  [3:0] IO_DATA_in,
  output [3:0] IO_DATA_out
);

  wire [3:0] stack_1_d0, stack_1_d1, stack_1_d2, stack_1_d3, stack_1_d4;

  // Probe on stack_1_d0
  stack stack_1 (
    .CLK(CLK), .RESET(RESET), .COMMAND(COMMAND), .INDEX(INDEX), .IO_DATA_in(IO_DATA_in), .d0(stack_1_d0),
    .d1(stack_1_d1), .d2(stack_1_d2), .d3(stack_1_d3), .d4(stack_1_d4), .IO_DATA_out(IO_DATA_out));
  // Probe on stack_1_d1
  // Probe on stack_1_d2
  // Probe on stack_1_d3
  // Probe on stack_1_d4
endmodule

module stack (
  input  CLK,
  input  RESET,
  input  [1:0] COMMAND,
  input  [2:0] INDEX,
  input  [3:0] IO_DATA_in,
  output [3:0] d0,
  output [3:0] d1,
  output [3:0] d2,
  output [3:0] d3,
  output [3:0] d4,
  output [3:0] IO_DATA_out
);

  wire demux_2x4_1_y0, demux_2x4_1_y1, demux_2x4_1_y2, demux_2x4_1_y3, or_1_out, or_2_out, por_1_out;
  wire [3:0] dec_mod5_1_data_out, demux_4x16_mod5_1_data_mod5, in_out_1_data_out, in_out_2_data_out,
       in_out_3_data_out, or_3_out, stack_header_1_index, subtract_4bit_1_diff;

  POR por_1 (.out(por_1_out));
  or or_1 (or_1_out, RESET, por_1_out);
  // NoConnect on demux_2x4_1_y0
  demux_2x4 demux_2x4_1 (
    .D(1'b1), .DATA_IN(COMMAND), .Y0(demux_2x4_1_y0), .Y1(demux_2x4_1_y1), .Y2(demux_2x4_1_y2),
    .Y3(demux_2x4_1_y3));
  or or_2 (or_2_out, demux_2x4_1_y2, demux_2x4_1_y3);
  stack_header stack_header_1 (
    .PUSH(demux_2x4_1_y1), .POP(demux_2x4_1_y2), .CLK(CLK), .RESET(or_1_out), .INDEX(stack_header_1_index));
  in_out in_out_1 (.DATA_IN({1'b0, INDEX}), .D(demux_2x4_1_y3), .DATA_OUT(in_out_1_data_out));
  subtract_4bit subtract_4bit_1 (.A(stack_header_1_index), .B(in_out_1_data_out), .diff(subtract_4bit_1_diff));
  dec_mod5 dec_mod5_1 (.DATA_IN(subtract_4bit_1_diff), .DATA_OUT(dec_mod5_1_data_out));
  // NoConnect on demux_4x16_mod5_1_data_mod5[3]
  demux_4x16_mod5 demux_4x16_mod5_1 (.DATA_IN(or_3_out), .DATA_mod5(demux_4x16_mod5_1_data_mod5));
  in_out in_out_2 (.DATA_IN(subtract_4bit_1_diff), .D(demux_2x4_1_y1), .DATA_OUT(in_out_2_data_out));
  in_out in_out_3 (.DATA_IN(dec_mod5_1_data_out), .D(or_2_out), .DATA_OUT(in_out_3_data_out));
  stack_memory stack_memory_1 (
    .GET(or_2_out), .INDEX(demux_4x16_mod5_1_data_mod5[2:0]), .CLK(CLK), .SET(demux_2x4_1_y1),
    .RESET(or_1_out), .IO_in(IO_DATA_in), .d0(d0), .d1(d1), .d2(d2), .d3(d3), .d4(d4), .IO_out(IO_DATA_in));
  assign or_3_out = in_out_2_data_out | in_out_3_data_out;  // OR_Gate or_3, 4 bits wide

  assign IO_DATA_out = IO_DATA_in;

  // Notes on the sheet:
  //   nop
  //   push
  //   pop
  //   get
endmodule

module rs_trigger (
  input  R,
  input  CLK,
  input  S,
  output Q,
  output Qi
);

  wire and_1_out, and_2_out, or_1_out, por_1_out;

  POR por_1 (.out(por_1_out));
  and and_1 (and_1_out, R, CLK);
  and and_2 (and_2_out, CLK, S);
  or or_1 (or_1_out, and_2_out, por_1_out);
  nor nor_1 (Q, and_1_out, Qi);
  nor nor_2 (Qi, Q, or_1_out);
endmodule

module d_trigger (
  input  D,
  input  CLK,
  output Q
);

  wire not_1_out, rs_trigger_1_qi;

  not not_1 (not_1_out, D);
  rs_trigger rs_trigger_1 (.R(not_1_out), .CLK(CLK), .S(D), .Q(Q), .Qi(rs_trigger_1_qi));
  // NoConnect on rs_trigger_1_qi
endmodule

module d_trigger_bk (
  input  D,
  input  CLK,
  output Q
);

  wire not_1_out, not_2_out, rs_trigger_1_q, rs_trigger_1_qi, rs_trigger_2_qi;

  not not_1 (not_1_out, D);
  not not_2 (not_2_out, CLK);
  rs_trigger rs_trigger_1 (.R(D), .CLK(CLK), .S(not_1_out), .Q(rs_trigger_1_q), .Qi(rs_trigger_1_qi));
  rs_trigger rs_trigger_2 (.R(rs_trigger_1_q), .CLK(not_2_out), .S(rs_trigger_1_qi), .Q(Q), .Qi(rs_trigger_2_qi));
  // NoConnect on rs_trigger_2_qi
endmodule

module RAM_4bit (
  input  [3:0] DATA_IN,
  input  CLK,
  output [3:0] DATA_OUT
);

  d_trigger d_trigger_1 (.D(DATA_IN[0]), .CLK(CLK), .Q(DATA_OUT[0]));
  d_trigger d_trigger_2 (.D(DATA_IN[1]), .CLK(CLK), .Q(DATA_OUT[1]));
  d_trigger d_trigger_3 (.D(DATA_IN[2]), .CLK(CLK), .Q(DATA_OUT[2]));
  d_trigger d_trigger_4 (.D(DATA_IN[3]), .CLK(CLK), .Q(DATA_OUT[3]));
endmodule

module RAM_4bit_bk (
  input  [3:0] DATA_IN,
  input  CLK,
  output [3:0] DATA_OUT
);

  d_trigger_bk d_trigger_bk_1 (.D(DATA_IN[0]), .CLK(CLK), .Q(DATA_OUT[0]));
  d_trigger_bk d_trigger_bk_2 (.D(DATA_IN[1]), .CLK(CLK), .Q(DATA_OUT[1]));
  d_trigger_bk d_trigger_bk_3 (.D(DATA_IN[2]), .CLK(CLK), .Q(DATA_OUT[2]));
  d_trigger_bk d_trigger_bk_4 (.D(DATA_IN[3]), .CLK(CLK), .Q(DATA_OUT[3]));
endmodule

module summ_1bit (
  input  C_in,
  input  A,
  input  B,
  output C_out,
  output S
);

  wire and_1_out, and_2_out, and_3_out;

  and and_1 (and_1_out, C_in, B);
  and and_2 (and_2_out, C_in, A);
  and and_3 (and_3_out, A, B);
  or or_1 (C_out, and_1_out, and_2_out, and_3_out);
  xor xor_1 (S, C_in, A, B);
endmodule

module summ_4bit (
  input  [3:0] A,
  input  [3:0] B,
  output [3:0] S
);

  wire summ_1bit_1_c_out, summ_1bit_2_c_out, summ_1bit_3_c_out, summ_1bit_4_c_out, undriven;

  // NoConnect on undriven
  summ_1bit summ_1bit_1 (.C_in(undriven), .A(A[0]), .B(B[0]), .C_out(summ_1bit_1_c_out), .S(S[0]));
  summ_1bit summ_1bit_2 (.C_in(summ_1bit_1_c_out), .A(A[1]), .B(B[1]), .C_out(summ_1bit_2_c_out), .S(S[1]));
  summ_1bit summ_1bit_3 (.C_in(summ_1bit_2_c_out), .A(A[2]), .B(B[2]), .C_out(summ_1bit_3_c_out), .S(S[2]));
  // NoConnect on summ_1bit_4_c_out
  summ_1bit summ_1bit_4 (.C_in(summ_1bit_3_c_out), .A(A[3]), .B(B[3]), .C_out(summ_1bit_4_c_out), .S(S[3]));
endmodule

module subtract_4bit (
  input  [3:0] A,
  input  [3:0] B,
  output [3:0] diff
);

  wire [3:0] not_1_out, summ_4bit_1_s, summ_4bit_2_s;

  assign not_1_out = ~B;  // NOT_Gate not_1, 4 bits wide
  summ_4bit summ_4bit_1 (.A(A), .B(4'b0101), .S(summ_4bit_1_s));
  summ_4bit summ_4bit_2 (.A(summ_4bit_1_s), .B(not_1_out), .S(summ_4bit_2_s));
  summ_4bit summ_4bit_3 (.A(summ_4bit_2_s), .B(4'b0001), .S(diff));
endmodule

module demux_2x4 (
  input  D,
  input  [1:0] DATA_IN,
  output Y0,
  output Y1,
  output Y2,
  output Y3
);

  wire not_1_out, not_2_out;

  not not_1 (not_1_out, DATA_IN[0]);
  not not_2 (not_2_out, DATA_IN[1]);
  and and_1 (Y0, D, not_1_out, not_2_out);
  and and_2 (Y1, D, DATA_IN[0], not_2_out);
  and and_3 (Y2, D, not_1_out, DATA_IN[1]);
  and and_4 (Y3, D, DATA_IN[0], DATA_IN[1]);
endmodule

module demux_3x8 (
  input  [2:0] DATA_IN,
  input  D,
  output Y0,
  output Y1,
  output Y2,
  output Y3,
  output Y4,
  output Y5,
  output Y6,
  output Y7
);

  wire and_1_out, and_2_out, not_1_out;

  not not_1 (not_1_out, DATA_IN[2]);
  and and_1 (and_1_out, not_1_out, D);
  and and_2 (and_2_out, DATA_IN[2], D);
  demux_2x4 demux_2x4_1 (.D(and_1_out), .DATA_IN(DATA_IN[1:0]), .Y0(Y0), .Y1(Y1), .Y2(Y2), .Y3(Y3));
  demux_2x4 demux_2x4_2 (.D(and_2_out), .DATA_IN(DATA_IN[1:0]), .Y0(Y4), .Y1(Y5), .Y2(Y6), .Y3(Y7));
endmodule

module demux_4x16_mod5 (
  input  [3:0] DATA_IN,
  output [3:0] DATA_mod5
);

  wire demux_3x8_1_y0, demux_3x8_1_y1, demux_3x8_1_y2, demux_3x8_1_y3, demux_3x8_1_y4, demux_3x8_1_y5,
       demux_3x8_1_y6, demux_3x8_1_y7, demux_3x8_2_y0, demux_3x8_2_y1, demux_3x8_2_y2, demux_3x8_2_y3,
       demux_3x8_2_y4, demux_3x8_2_y5, demux_3x8_2_y6, demux_3x8_2_y7, not_1_out;
  wire [3:0] in_out_1_data_out, in_out_2_data_out, in_out_3_data_out, in_out_4_data_out, in_out_5_data_out,
       in_out_6_data_out, in_out_7_data_out, in_out_8_data_out, in_out_9_data_out, in_out_10_data_out,
       in_out_11_data_out, in_out_12_data_out, in_out_13_data_out, in_out_14_data_out, in_out_15_data_out,
       in_out_16_data_out, or_1_out, or_2_out, or_3_out, or_4_out, or_5_out, or_6_out, or_7_out, or_8_out,
       or_9_out, or_10_out, or_11_out, or_12_out, or_13_out, or_14_out;

  not not_1 (not_1_out, DATA_IN[3]);
  demux_3x8 demux_3x8_1 (
    .DATA_IN(DATA_IN[2:0]), .D(not_1_out), .Y0(demux_3x8_1_y0), .Y1(demux_3x8_1_y1), .Y2(demux_3x8_1_y2),
    .Y3(demux_3x8_1_y3), .Y4(demux_3x8_1_y4), .Y5(demux_3x8_1_y5), .Y6(demux_3x8_1_y6), .Y7(demux_3x8_1_y7));
  demux_3x8 demux_3x8_2 (
    .DATA_IN(DATA_IN[2:0]), .D(DATA_IN[3]), .Y0(demux_3x8_2_y0), .Y1(demux_3x8_2_y1), .Y2(demux_3x8_2_y2),
    .Y3(demux_3x8_2_y3), .Y4(demux_3x8_2_y4), .Y5(demux_3x8_2_y5), .Y6(demux_3x8_2_y6), .Y7(demux_3x8_2_y7));
  in_out in_out_1 (.DATA_IN(4'b0000), .D(demux_3x8_1_y0), .DATA_OUT(in_out_1_data_out));
  in_out in_out_2 (.DATA_IN(4'b0001), .D(demux_3x8_1_y1), .DATA_OUT(in_out_2_data_out));
  in_out in_out_3 (.DATA_IN(4'b0010), .D(demux_3x8_1_y2), .DATA_OUT(in_out_3_data_out));
  in_out in_out_4 (.DATA_IN(4'b0011), .D(demux_3x8_1_y3), .DATA_OUT(in_out_4_data_out));
  in_out in_out_5 (.DATA_IN(4'b0100), .D(demux_3x8_1_y4), .DATA_OUT(in_out_5_data_out));
  in_out in_out_6 (.DATA_IN(4'b0000), .D(demux_3x8_1_y5), .DATA_OUT(in_out_6_data_out));
  in_out in_out_7 (.DATA_IN(4'b0001), .D(demux_3x8_1_y6), .DATA_OUT(in_out_7_data_out));
  in_out in_out_8 (.DATA_IN(4'b0010), .D(demux_3x8_1_y7), .DATA_OUT(in_out_8_data_out));
  in_out in_out_9 (.DATA_IN(4'b0011), .D(demux_3x8_2_y0), .DATA_OUT(in_out_9_data_out));
  in_out in_out_10 (.DATA_IN(4'b0100), .D(demux_3x8_2_y1), .DATA_OUT(in_out_10_data_out));
  in_out in_out_11 (.DATA_IN(4'b0000), .D(demux_3x8_2_y2), .DATA_OUT(in_out_11_data_out));
  in_out in_out_12 (.DATA_IN(4'b0001), .D(demux_3x8_2_y3), .DATA_OUT(in_out_12_data_out));
  in_out in_out_13 (.DATA_IN(4'b0010), .D(demux_3x8_2_y4), .DATA_OUT(in_out_13_data_out));
  in_out in_out_14 (.DATA_IN(4'b0011), .D(demux_3x8_2_y5), .DATA_OUT(in_out_14_data_out));
  in_out in_out_15 (.DATA_IN(4'b0100), .D(demux_3x8_2_y6), .DATA_OUT(in_out_15_data_out));
  in_out in_out_16 (.DATA_IN(4'b0000), .D(demux_3x8_2_y7), .DATA_OUT(in_out_16_data_out));
  assign or_1_out = in_out_1_data_out | in_out_2_data_out;  // OR_Gate or_1, 4 bits wide
  assign or_2_out = in_out_3_data_out | in_out_4_data_out;  // OR_Gate or_2, 4 bits wide
  assign or_3_out = in_out_5_data_out | in_out_6_data_out;  // OR_Gate or_3, 4 bits wide
  assign or_4_out = in_out_7_data_out | in_out_8_data_out;  // OR_Gate or_4, 4 bits wide
  assign or_5_out = in_out_9_data_out | in_out_10_data_out;  // OR_Gate or_5, 4 bits wide
  assign or_6_out = in_out_11_data_out | in_out_12_data_out;  // OR_Gate or_6, 4 bits wide
  assign or_7_out = in_out_13_data_out | in_out_14_data_out;  // OR_Gate or_7, 4 bits wide
  assign or_8_out = in_out_15_data_out | in_out_16_data_out;  // OR_Gate or_8, 4 bits wide
  assign or_9_out = or_1_out | or_2_out;  // OR_Gate or_9, 4 bits wide
  assign or_10_out = or_3_out | or_4_out;  // OR_Gate or_10, 4 bits wide
  assign or_11_out = or_5_out | or_6_out;  // OR_Gate or_11, 4 bits wide
  assign or_12_out = or_7_out | or_8_out;  // OR_Gate or_12, 4 bits wide
  assign or_13_out = or_9_out | or_10_out;  // OR_Gate or_13, 4 bits wide
  assign or_14_out = or_11_out | or_12_out;  // OR_Gate or_14, 4 bits wide
  assign DATA_mod5 = or_13_out | or_14_out;  // OR_Gate or_15, 4 bits wide
endmodule

module in_out (
  input  [3:0] DATA_IN,
  input  D,
  output [3:0] DATA_OUT
);

  and and_1 (DATA_OUT[0], DATA_IN[0], D);
  and and_2 (DATA_OUT[1], DATA_IN[1], D);
  and and_3 (DATA_OUT[2], DATA_IN[2], D);
  and and_4 (DATA_OUT[3], DATA_IN[3], D);
endmodule

module inc_mod5 (
  input  [3:0] DATA_IN,
  output [3:0] DATA_OUT
);

  wire and_1_out, not_1_out;
  wire [3:0] in_out_1_data_out, in_out_2_data_out, or_1_out, summ_4bit_1_s;

  and and_1 (and_1_out, DATA_IN[0], DATA_IN[1], DATA_IN[2], DATA_IN[3]);
  not not_1 (not_1_out, and_1_out);
  in_out in_out_1 (.DATA_IN(DATA_IN), .D(not_1_out), .DATA_OUT(in_out_1_data_out));
  in_out in_out_2 (.DATA_IN(4'b0000), .D(and_1_out), .DATA_OUT(in_out_2_data_out));
  assign or_1_out = in_out_1_data_out | in_out_2_data_out;  // OR_Gate or_1, 4 bits wide
  summ_4bit summ_4bit_1 (.A(or_1_out), .B(4'b0001), .S(summ_4bit_1_s));
  demux_4x16_mod5 demux_4x16_mod5_1 (.DATA_IN(summ_4bit_1_s), .DATA_mod5(DATA_OUT));
endmodule

module dec_mod5 (
  input  [3:0] DATA_IN,
  output [3:0] DATA_OUT
);

  wire and_1_out, not_1_out;
  wire [3:0] in_out_1_data_out, in_out_2_data_out, or_1_out, subtract_4bit_1_diff;

  and and_1 (and_1_out, ~DATA_IN[0], ~DATA_IN[1], ~DATA_IN[2], ~DATA_IN[3]);  // AND_Gate
  not not_1 (not_1_out, and_1_out);
  in_out in_out_1 (.DATA_IN(DATA_IN), .D(not_1_out), .DATA_OUT(in_out_1_data_out));
  in_out in_out_2 (.DATA_IN(4'b0101), .D(and_1_out), .DATA_OUT(in_out_2_data_out));
  assign or_1_out = in_out_1_data_out | in_out_2_data_out;  // OR_Gate or_1, 4 bits wide
  subtract_4bit subtract_4bit_1 (.A(or_1_out), .B(4'b0001), .diff(subtract_4bit_1_diff));
  demux_4x16_mod5 demux_4x16_mod5_1 (.DATA_IN(subtract_4bit_1_diff), .DATA_mod5(DATA_OUT));
endmodule

module stack_header (
  input  PUSH,
  input  POP,
  input  CLK,
  input  RESET,
  output [3:0] INDEX
);

  wire and_1_out, not_1_out, or_1_out, or_2_out;
  wire [3:0] dec_mod5_1_data_out, in_out_1_data_out, in_out_2_data_out, in_out_3_data_out,
       inc_mod5_1_data_out, or_3_out;

  or or_1 (or_1_out, PUSH, POP);
  and and_1 (and_1_out, or_1_out, CLK);
  inc_mod5 inc_mod5_1 (.DATA_IN(INDEX), .DATA_OUT(inc_mod5_1_data_out));
  dec_mod5 dec_mod5_1 (.DATA_IN(INDEX), .DATA_OUT(dec_mod5_1_data_out));
  or or_2 (or_2_out, and_1_out, RESET);
  in_out in_out_1 (.DATA_IN(inc_mod5_1_data_out), .D(PUSH), .DATA_OUT(in_out_1_data_out));
  in_out in_out_2 (.DATA_IN(dec_mod5_1_data_out), .D(POP), .DATA_OUT(in_out_2_data_out));
  assign or_3_out = in_out_1_data_out | in_out_2_data_out;  // OR_Gate or_3, 4 bits wide
  not not_1 (not_1_out, RESET);
  in_out in_out_3 (.DATA_IN(or_3_out), .D(not_1_out), .DATA_OUT(in_out_3_data_out));
  RAM_4bit_bk ram_4bit_bk_1 (.DATA_IN(in_out_3_data_out), .CLK(or_2_out), .DATA_OUT(INDEX));
endmodule

module stack_memory (
  input  GET,
  input  [2:0] INDEX,
  input  CLK,
  input  SET,
  input  RESET,
  input  [3:0] IO_in,
  output [3:0] d0,
  output [3:0] d1,
  output [3:0] d2,
  output [3:0] d3,
  output [3:0] d4,
  output [3:0] IO_out
);

  wire and_1_out, and_2_out, and_3_out, and_4_out, and_5_out, and_6_out, demux_3x8_1_y0, demux_3x8_1_y1,
       demux_3x8_1_y2, demux_3x8_1_y3, demux_3x8_1_y4, demux_3x8_2_y0, demux_3x8_2_y1, demux_3x8_2_y2,
       demux_3x8_2_y3, demux_3x8_2_y4, not_1_out, or_1_out, or_2_out, or_3_out, or_4_out, or_5_out, or_6_out,
       por_1_out;
  wire [3:0] in_out_1_data_out, in_out_2_data_out, in_out_3_data_out, in_out_4_data_out, in_out_5_data_out,
       in_out_6_data_out, or_7_out;

  or or_1 (or_1_out, RESET, por_1_out);
  POR por_1 (.out(por_1_out));
  not not_1 (not_1_out, or_1_out);
  demux_3x8 demux_3x8_1 (
    .DATA_IN(INDEX), .D(SET), .Y0(demux_3x8_1_y0), .Y1(demux_3x8_1_y1), .Y2(demux_3x8_1_y2),
    .Y3(demux_3x8_1_y3), .Y4(demux_3x8_1_y4));  // open: Y5, Y6, Y7
  in_out in_out_1 (.DATA_IN(IO_in), .D(not_1_out), .DATA_OUT(in_out_1_data_out));
  and and_1 (and_1_out, demux_3x8_1_y0, CLK);
  and and_2 (and_2_out, CLK, demux_3x8_1_y1);
  and and_3 (and_3_out, CLK, demux_3x8_1_y2);
  and and_4 (and_4_out, CLK, demux_3x8_1_y3);
  and and_5 (and_5_out, CLK, demux_3x8_1_y4);
  or or_2 (or_2_out, and_1_out, or_1_out);
  or or_3 (or_3_out, and_2_out, or_1_out);
  or or_4 (or_4_out, and_3_out, or_1_out);
  or or_5 (or_5_out, and_4_out, or_1_out);
  or or_6 (or_6_out, and_5_out, or_1_out);
  demux_3x8 demux_3x8_2 (
    .DATA_IN(INDEX), .D(GET), .Y0(demux_3x8_2_y0), .Y1(demux_3x8_2_y1), .Y2(demux_3x8_2_y2),
    .Y3(demux_3x8_2_y3), .Y4(demux_3x8_2_y4));  // open: Y5, Y6, Y7
  and and_6 (and_6_out, GET, CLK);
  RAM_4bit ram_4bit_1 (.DATA_IN(in_out_1_data_out), .CLK(or_2_out), .DATA_OUT(d0));
  RAM_4bit ram_4bit_2 (.DATA_IN(in_out_1_data_out), .CLK(or_3_out), .DATA_OUT(d1));
  RAM_4bit ram_4bit_3 (.DATA_IN(in_out_1_data_out), .CLK(or_4_out), .DATA_OUT(d2));
  RAM_4bit ram_4bit_4 (.DATA_IN(in_out_1_data_out), .CLK(or_5_out), .DATA_OUT(d3));
  RAM_4bit ram_4bit_5 (.DATA_IN(in_out_1_data_out), .CLK(or_6_out), .DATA_OUT(d4));
  in_out in_out_2 (.DATA_IN(d0), .D(demux_3x8_2_y0), .DATA_OUT(in_out_2_data_out));
  in_out in_out_3 (.DATA_IN(d1), .D(demux_3x8_2_y1), .DATA_OUT(in_out_3_data_out));
  in_out in_out_4 (.DATA_IN(d2), .D(demux_3x8_2_y2), .DATA_OUT(in_out_4_data_out));
  in_out in_out_5 (.DATA_IN(d3), .D(demux_3x8_2_y3), .DATA_OUT(in_out_5_data_out));
  in_out in_out_6 (.DATA_IN(d4), .D(demux_3x8_2_y4), .DATA_OUT(in_out_6_data_out));
  assign or_7_out = in_out_2_data_out | in_out_3_data_out | in_out_4_data_out | in_out_5_data_out | in_out_6_data_out;  // OR_Gate or_7, 4 bits wide
  ventil_4bit ventil_4bit_1 (.DATA_IN(or_7_out), .D(and_6_out), .DATA_OUT(IO_out));
endmodule

module ventil_1bit (
  input  D,
  input  I,
  output O
);

  wire not_1_out;

  not not_1 (not_1_out, D);
  // Transmission_Gate transmission_1: pin names not known; wires that end beside it: I, not_1_out, D, O
endmodule

module ventil_4bit (
  input  [3:0] DATA_IN,
  input  D,
  output [3:0] DATA_OUT
);

  ventil_1bit ventil_1bit_1 (.D(D), .I(DATA_IN[0]), .O(DATA_OUT[0]));
  ventil_1bit ventil_1bit_2 (.D(D), .I(DATA_IN[1]), .O(DATA_OUT[1]));
  ventil_1bit ventil_1bit_3 (.D(D), .I(DATA_IN[2]), .O(DATA_OUT[2]));
  ventil_1bit ventil_1bit_4 (.D(D), .I(DATA_IN[3]), .O(DATA_OUT[3]));
endmodule
